// Logisim project adder.circ as structural Verilog
module adder1bit (
  input  a,
  input  b,
  input  c,
  output h,
  output f
);

  wire nand_1_out, nand_3_out, nand_4_out, nand_5_out, nand_6_out, nand_7_out, nand_9_out;

  nand nand_1 (nand_1_out, a, nand_6_out);
  nand nand_2 (h, nand_3_out, nand_6_out);
  nand nand_3 (nand_3_out, b, c);
  nand nand_4 (nand_4_out, b, nand_3_out);
  nand nand_5 (nand_5_out, nand_4_out, nand_9_out);
  nand nand_6 (nand_6_out, a, nand_5_out);
  nand nand_7 (nand_7_out, nand_6_out, nand_5_out);
  nand nand_8 (f, nand_1_out, nand_7_out);
  nand nand_9 (nand_9_out, nand_3_out, c);
endmodule

module adder4bit (
  input  a3,
  input  a2,
  input  a1,
  input  a0,
  input  b3,
  input  b2,
  input  b1,
  input  b0,
  input  c,
  output c_2,
  output f3,
  output f2,
  output f1,
  output f0
);

  wire adder1bit_2_h, adder1bit_3_h, adder1bit_4_h;

  adder1bit adder1bit_1 (.a(a3), .b(b3), .c(adder1bit_4_h), .h(c_2), .f(f3));
  adder1bit adder1bit_2 (.a(a0), .b(b0), .c(c), .h(adder1bit_2_h), .f(f0));
  adder1bit adder1bit_3 (.a(a1), .b(b1), .c(adder1bit_2_h), .h(adder1bit_3_h), .f(f1));
  adder1bit adder1bit_4 (.a(a2), .b(b2), .c(adder1bit_3_h), .h(adder1bit_4_h), .f(f2));
endmodule
