// Logisim project doubledabble.circ as structural Verilog
module singlelayer (
  input  a3,
  input  a2,
  input  a1,
  input  a0,
  output f3,
  output f2,
  output f1,
  output f0
);

  wire adder4bit_1_f0, adder4bit_1_f1, adder4bit_1_f2, adder4bit_1_f3, and_1_out, and_2_out, and_3_out,
       and_4_out, and_5_out, and_6_out, and_7_out, and_8_out, and_9_out, not_1_out, or_1_out, or_2_out;

  or or_1 (or_1_out, a0, a1);
  and and_1 (and_1_out, or_1_out, a2);
  or or_2 (or_2_out, a3, and_1_out);
  not not_1 (not_1_out, or_2_out);
  adder4bit adder4bit_1 (
    .a3(a3), .a2(a2), .a1(a1), .a0(a0), .b3(1'b0), .b2(1'b0), .b1(1'b1), .b0(1'b1), .c(1'b0),
    .f3(adder4bit_1_f3), .f2(adder4bit_1_f2), .f1(adder4bit_1_f1), .f0(adder4bit_1_f0));  // open: c_2
  and and_2 (and_2_out, adder4bit_1_f0, or_2_out);
  or or_3 (f0, and_2_out, and_3_out);
  and and_3 (and_3_out, a0, not_1_out);
  and and_4 (and_4_out, adder4bit_1_f1, or_2_out);
  or or_4 (f1, and_4_out, and_5_out);
  and and_5 (and_5_out, a1, not_1_out);
  and and_6 (and_6_out, adder4bit_1_f2, or_2_out);
  or or_5 (f2, and_6_out, and_7_out);
  and and_7 (and_7_out, a2, not_1_out);
  and and_8 (and_8_out, adder4bit_1_f3, or_2_out);
  or or_6 (f3, and_8_out, and_9_out);
  and and_9 (and_9_out, a3, not_1_out);
endmodule

module doubledabble (
  input  a4,
  input  a3,
  input  a2,
  input  a1,
  input  a0,
  output f3,
  output f2,
  output f1,
  output f0,
  output g3,
  output g2,
  output g1,
  output g0
);

  wire singlelayer_1_f0, singlelayer_1_f1, singlelayer_1_f2;

  singlelayer singlelayer_1 (
    .a3(1'b0), .a2(a4), .a1(a3), .a0(a2), .f3(f1), .f2(singlelayer_1_f2), .f1(singlelayer_1_f1),
    .f0(singlelayer_1_f0));
  singlelayer singlelayer_2 (
    .a3(singlelayer_1_f2), .a2(singlelayer_1_f1), .a1(singlelayer_1_f0), .a0(a1), .f3(f0), .f2(g3), .f1(g2),
    .f0(g1));

  assign f2 = 1'b0;
  assign f3 = 1'b0;
  assign g0 = a0;
endmodule
