// Logisim project multiplexer.circ as structural Verilog
module multiplexer2way (
  input  w,
  input  S,
  input  x,
  output out
);

  wire and_1_out, and_2_out, not_1_out;

  not not_1 (not_1_out, S);
  and and_1 (and_1_out, w, not_1_out);
  and and_2 (and_2_out, S, x);
  or or_1 (out, and_1_out, and_2_out);
endmodule

module multiplexer4way (
  input  in_1,
  input  in_2,
  input  w,
  input  x,
  input  y,
  input  z,
  output out_7
);

  wire multiplexer2way_1_out, multiplexer2way_2_out;

  multiplexer2way multiplexer2way_1 (.w(w), .x(x), .S(in_2), .out(multiplexer2way_1_out));
  multiplexer2way multiplexer2way_2 (.w(y), .x(z), .S(in_2), .out(multiplexer2way_2_out));
  multiplexer2way multiplexer2way_3 (.w(multiplexer2way_1_out), .x(multiplexer2way_2_out), .S(in_1), .out(out_7));
endmodule

module multiplexer4way4bit (
  input  in_1,
  input  in_2,
  input  in_3,
  input  in_4,
  input  in_5,
  input  in_6,
  input  in_7,
  input  in_8,
  input  in_9,
  input  in_10,
  input  in_11,
  input  in_12,
  input  in_13,
  input  in_14,
  input  in_15,
  input  in_16,
  input  in_17,
  input  in_18,
  output out_19,
  output out_20,
  output out_21,
  output out_22
);

  multiplexer4way multiplexer4way_1 (
    .w(in_6), .x(in_10), .y(in_14), .z(in_18), .in_1(in_1), .in_2(in_2), .out_7(out_22));
  multiplexer4way multiplexer4way_2 (
    .w(in_4), .x(in_8), .y(in_12), .z(in_16), .in_1(in_1), .in_2(in_2), .out_7(out_20));
  multiplexer4way multiplexer4way_3 (
    .w(in_5), .x(in_9), .y(in_13), .z(in_17), .in_1(in_1), .in_2(in_2), .out_7(out_21));
  multiplexer4way multiplexer4way_4 (
    .w(in_3), .x(in_7), .y(in_11), .z(in_15), .in_1(in_1), .in_2(in_2), .out_7(out_19));
endmodule
