// Logisim project project2_main.circ as structural Verilog: 1 circuit, main circuit main
module main (
  input  LS,
  input  A0,
  input  MS,
  input  in_4,
  input  in_5,
  input  in_6,
  input  in_7,
  input  in_8,
  input  A1,
  input  in_10,
  input  in_11,
  input  in_12,
  input  in_13,
  input  A2,
  input  in_15,
  input  in_16,
  input  in_17,
  input  A3,
  input  in_19,
  input  in_20,
  input  B0,
  input  in_22,
  input  in_23,
  input  in_24,
  input  in_25,
  input  B1,
  input  in_27,
  input  in_28,
  input  in_29,
  input  B2,
  input  in_31,
  input  in_32,
  input  in_33,
  input  B3,
  input  in_35,
  input  in_36
);

  wire adder4bit_1_c_2, adder4bit_1_f0, adder4bit_1_f1, adder4bit_1_f2, adder4bit_1_f3, doubledabble_1_f0,
       doubledabble_1_f1, doubledabble_1_f2, doubledabble_1_f3, doubledabble_1_g0, doubledabble_1_g1,
       doubledabble_1_g2, doubledabble_1_g3, hex_7seg_driver_1_p4, hex_7seg_driver_1_p5,
       hex_7seg_driver_1_p6, hex_7seg_driver_1_p7, hex_7seg_driver_2_p6, hex_7seg_driver_2_p7,
       hex_7seg_driver_2_p8, hex_7seg_driver_2_p9, hex_7seg_driver_2_p10, hex_7seg_driver_2_p11,
       hex_7seg_driver_2_p12, hex_7seg_driver_2_p13, hex_7seg_driver_2_p14, hex_7seg_driver_2_p15,
       hex_7seg_driver_3_p4, hex_7seg_driver_3_p5, hex_7seg_driver_3_p6, hex_7seg_driver_3_p7,
       hex_7seg_driver_4_p6, hex_7seg_driver_4_p7, hex_7seg_driver_4_p8, hex_7seg_driver_4_p9,
       hex_7seg_driver_4_p10, hex_7seg_driver_4_p11, hex_7seg_driver_4_p12, hex_7seg_driver_4_p13,
       hex_7seg_driver_4_p14, hex_7seg_driver_4_p15, multiplexer4way4bit_1_out_19,
       multiplexer4way4bit_1_out_20, multiplexer4way4bit_1_out_21, multiplexer4way4bit_1_out_22,
       multiplexer4way4bit_2_out_19, multiplexer4way4bit_2_out_20, multiplexer4way4bit_2_out_21,
       multiplexer4way4bit_2_out_22;

  multiplexer4way4bit multiplexer4way4bit_1 (
    .in_3(LS), .in_4(A0), .in_5(MS), .in_6(in_8), .in_7(A1), .in_8(in_10), .in_9(in_11), .in_10(in_12),
    .in_11(in_13), .in_12(A2), .in_13(in_15), .in_14(in_16), .in_15(in_17), .in_16(A3), .in_17(in_19),
    .in_18(in_20), .in_1(in_4), .in_2(in_5), .out_19(multiplexer4way4bit_1_out_19),
    .out_20(multiplexer4way4bit_1_out_20), .out_21(multiplexer4way4bit_1_out_21),
    .out_22(multiplexer4way4bit_1_out_22));
  multiplexer4way4bit multiplexer4way4bit_2 (
    .in_3(B0), .in_4(in_22), .in_5(in_23), .in_6(in_24), .in_7(in_25), .in_8(B1), .in_9(in_27),
    .in_10(in_28), .in_11(in_29), .in_12(B2), .in_13(in_31), .in_14(in_32), .in_15(in_33), .in_16(B3),
    .in_17(in_35), .in_18(in_36), .in_1(in_6), .in_2(in_7), .out_19(multiplexer4way4bit_2_out_19),
    .out_20(multiplexer4way4bit_2_out_20), .out_21(multiplexer4way4bit_2_out_21),
    .out_22(multiplexer4way4bit_2_out_22));
  adder4bit adder4bit_1 (
    .a3(multiplexer4way4bit_1_out_22), .a2(multiplexer4way4bit_1_out_21), .a1(multiplexer4way4bit_1_out_20),
    .a0(multiplexer4way4bit_1_out_19), .b3(multiplexer4way4bit_2_out_22), .b2(multiplexer4way4bit_2_out_21),
    .b1(multiplexer4way4bit_2_out_20), .b0(multiplexer4way4bit_2_out_19), .c(1'b0), .c_2(adder4bit_1_c_2),
    .f3(adder4bit_1_f3), .f2(adder4bit_1_f2), .f1(adder4bit_1_f1), .f0(adder4bit_1_f0));
  doubledabble doubledabble_1 (
    .a4(adder4bit_1_c_2), .a3(adder4bit_1_f3), .a2(adder4bit_1_f2), .a1(adder4bit_1_f1), .a0(adder4bit_1_f0),
    .f3(doubledabble_1_f3), .f2(doubledabble_1_f2), .f1(doubledabble_1_f1), .f0(doubledabble_1_f0),
    .g3(doubledabble_1_g3), .g2(doubledabble_1_g2), .g1(doubledabble_1_g1), .g0(doubledabble_1_g0));
  // hex_7seg_driver hex_7seg_driver_1: pin names not known; wires that end beside it: multiplexer4way4bit_2_out_19, multiplexer4way4bit_2_out_20, multiplexer4way4bit_2_out_21, hex_7seg_driver_1_p4, hex_7seg_driver_1_p5, hex_7seg_driver_1_p6, hex_7seg_driver_1_p7
  // hex_7seg_driver hex_7seg_driver_2: pin names not known; wires that end beside it: multiplexer4way4bit_2_out_22, multiplexer4way4bit_1_out_19, multiplexer4way4bit_1_out_20, multiplexer4way4bit_1_out_21, multiplexer4way4bit_1_out_22, hex_7seg_driver_2_p6, hex_7seg_driver_2_p7, hex_7seg_driver_2_p8, hex_7seg_driver_2_p9, hex_7seg_driver_2_p10, hex_7seg_driver_2_p11, hex_7seg_driver_2_p12, hex_7seg_driver_2_p13, hex_7seg_driver_2_p14, hex_7seg_driver_2_p15
  // hex_7seg_driver hex_7seg_driver_3: pin names not known; wires that end beside it: doubledabble_1_g0, doubledabble_1_g1, doubledabble_1_g2, hex_7seg_driver_3_p4, hex_7seg_driver_3_p5, hex_7seg_driver_3_p6, hex_7seg_driver_3_p7
  // hex_7seg_driver hex_7seg_driver_4: pin names not known; wires that end beside it: doubledabble_1_g3, doubledabble_1_f0, doubledabble_1_f1, doubledabble_1_f2, doubledabble_1_f3, hex_7seg_driver_4_p6, hex_7seg_driver_4_p7, hex_7seg_driver_4_p8, hex_7seg_driver_4_p9, hex_7seg_driver_4_p10, hex_7seg_driver_4_p11, hex_7seg_driver_4_p12, hex_7seg_driver_4_p13, hex_7seg_driver_4_p14, hex_7seg_driver_4_p15
  _7_Segment_Display u_7_segment_display_1 (
    .g(hex_7seg_driver_2_p15), .f(hex_7seg_driver_2_p14), .a(hex_7seg_driver_2_p9),
    .b(hex_7seg_driver_2_p10), .e(hex_7seg_driver_2_p13), .d(hex_7seg_driver_2_p12), .c(hex_7seg_driver_2_p11));  // open: dp
  _7_Segment_Display u_7_segment_display_2 (
    .g(hex_7seg_driver_2_p8), .f(hex_7seg_driver_2_p7), .a(hex_7seg_driver_1_p4), .b(hex_7seg_driver_1_p5),
    .e(hex_7seg_driver_2_p6), .d(hex_7seg_driver_1_p7), .c(hex_7seg_driver_1_p6));  // open: dp
  _7_Segment_Display u_7_segment_display_3 (
    .g(hex_7seg_driver_4_p15), .f(hex_7seg_driver_4_p14), .a(hex_7seg_driver_4_p9),
    .b(hex_7seg_driver_4_p10), .e(hex_7seg_driver_4_p13), .d(hex_7seg_driver_4_p12), .c(hex_7seg_driver_4_p11));  // open: dp
  _7_Segment_Display u_7_segment_display_4 (
    .g(hex_7seg_driver_4_p8), .f(hex_7seg_driver_4_p7), .a(hex_7seg_driver_3_p4), .b(hex_7seg_driver_3_p5),
    .e(hex_7seg_driver_4_p6), .d(hex_7seg_driver_3_p7), .c(hex_7seg_driver_3_p6));  // open: dp

  // Notes on the sheet:
  //   +
  //   =
endmodule
